// Logisim project Relogio.circ as structural Verilog: 4 circuits, main circuit main
module main (
);

  wire AA, AB, AC, AD, AE, AF, AG, BA, BB, BC, BD, BE, BF, BG, CA, CB, CC, CD, CE, CF, CG, DA, DB, DC, DD,
       DE, DF, DG;

  _7_Segment_Display u_7_segment_display_1 (.g(BG), .f(BF), .a(BA), .b(BB), .e(BE), .d(BD), .c(BC));  // open: dp
  _7_Segment_Display u_7_segment_display_2 (.g(AG), .f(AF), .a(AA), .b(AB), .e(AE), .d(AD), .c(AC));  // open: dp
  contador contador_1 (
    .out_1({AG, AF, AE, AD, AC, AB, AA}), .out_2({BG, BF, BE, BD, BC, BB, BA}),
    .out_3({CG, CF, CE, CD, CC, CB, CA}), .out_4({DG, DF, DE, DD, DC, DB, DA}));  // open: out_5
  _7_Segment_Display u_7_segment_display_3 (.g(DG), .f(DF), .a(DA), .b(DB), .e(DE), .d(DD), .c(DC));  // open: dp
  _7_Segment_Display u_7_segment_display_4 (.g(CG), .f(CF), .a(CA), .b(CB), .e(CE), .d(CD), .c(CC));  // open: dp
endmodule

module Relogio (
);

  wire and_1_out, and_2_out, clock_1_out, clock_2_out, display_de_7_1_a_2, display_de_7_1_b_2,
       display_de_7_1_c_2, display_de_7_1_d_2, display_de_7_1_e, display_de_7_1_f, display_de_7_1_g,
       display_de_7_2_a_2, display_de_7_2_b_2, display_de_7_2_c_2, display_de_7_2_d_2, display_de_7_2_e,
       display_de_7_2_f, display_de_7_2_g, display_de_7_3_f, display_de_7_3_g, j_k_ff_1_q, j_k_ff_1_qn,
       j_k_ff_2_q, j_k_ff_2_qn, j_k_ff_3_q, j_k_ff_3_qn, j_k_ff_4_q, j_k_ff_5_q, j_k_ff_5_qn, j_k_ff_6_q,
       j_k_ff_6_qn, j_k_ff_7_q, j_k_ff_8_q, j_k_ff_8_qn, j_k_ff_9_q, j_k_ff_9_qn, j_k_ff_10_q, j_k_ff_10_qn,
       j_k_ff_11_q;

  Clock clock_1 (.out(clock_1_out));
  J_K_Flip_Flop j_k_ff_1 (
    .J(1'b1), .clk(clock_1_out), .K(1'b1), .Q(j_k_ff_1_q), .Qn(j_k_ff_1_qn), .reset(and_1_out));  // open: preset, en
  J_K_Flip_Flop j_k_ff_2 (
    .J(1'b1), .clk(j_k_ff_1_qn), .K(1'b1), .Q(j_k_ff_2_q), .Qn(j_k_ff_2_qn), .reset(and_1_out));  // open: preset, en
  J_K_Flip_Flop j_k_ff_3 (
    .J(1'b1), .clk(j_k_ff_2_qn), .K(1'b1), .Q(j_k_ff_3_q), .Qn(j_k_ff_3_qn), .reset(and_1_out));  // open: preset, en
  _7_Segment_Display u_7_segment_display_1 (
    .g(display_de_7_2_g), .f(display_de_7_2_f), .a(display_de_7_2_a_2), .b(display_de_7_2_b_2),
    .e(display_de_7_2_e), .d(display_de_7_2_d_2), .c(display_de_7_2_c_2));  // open: dp
  LED led_1 (.in(clock_2_out));
  LED led_2 (.in(clock_2_out));
  Clock clock_2 (.out(clock_2_out));
  display_de_7 display_de_7_1 (
    .a(j_k_ff_4_q), .b(j_k_ff_3_q), .c(j_k_ff_2_q), .d(j_k_ff_1_q), .a_2(display_de_7_1_a_2),
    .b_2(display_de_7_1_b_2), .c_2(display_de_7_1_c_2), .d_2(display_de_7_1_d_2), .e(display_de_7_1_e),
    .f(display_de_7_1_f), .g(display_de_7_1_g));
  J_K_Flip_Flop j_k_ff_4 (
    .J(1'b1), .clk(j_k_ff_3_qn), .K(1'b1), .Q(j_k_ff_4_q), .reset(and_1_out));  // open: Qn, preset, en
  and and_1 (and_1_out, j_k_ff_4_q, j_k_ff_2_q);
  _7_Segment_Display u_7_segment_display_2 (
    .g(display_de_7_1_g), .f(display_de_7_1_f), .a(display_de_7_1_a_2), .b(display_de_7_1_b_2),
    .e(display_de_7_1_e), .d(display_de_7_1_d_2), .c(display_de_7_1_c_2));  // open: dp
  J_K_Flip_Flop j_k_ff_5 (
    .J(1'b1), .clk(and_1_out), .K(1'b1), .Q(j_k_ff_5_q), .Qn(j_k_ff_5_qn), .reset(and_2_out));  // open: preset, en
  J_K_Flip_Flop j_k_ff_6 (
    .J(1'b1), .clk(j_k_ff_5_qn), .K(1'b1), .Q(j_k_ff_6_q), .Qn(j_k_ff_6_qn), .reset(and_2_out));  // open: preset, en
  J_K_Flip_Flop j_k_ff_7 (
    .J(1'b1), .clk(j_k_ff_6_qn), .K(1'b1), .Q(j_k_ff_7_q), .reset(and_2_out));  // open: Qn, preset, en
  and and_2 (and_2_out, j_k_ff_7_q, j_k_ff_6_q);
  display_de_7 display_de_7_2 (
    .a(1'b0), .b(j_k_ff_7_q), .c(j_k_ff_6_q), .d(j_k_ff_5_q), .a_2(display_de_7_2_a_2),
    .b_2(display_de_7_2_b_2), .c_2(display_de_7_2_c_2), .d_2(display_de_7_2_d_2), .e(display_de_7_2_e),
    .f(display_de_7_2_f), .g(display_de_7_2_g));
  J_K_Flip_Flop j_k_ff_8 (
    .J(1'b1), .clk(and_2_out), .K(1'b1), .Q(j_k_ff_8_q), .Qn(j_k_ff_8_qn));  // open: preset, en, reset
  J_K_Flip_Flop j_k_ff_9 (
    .J(1'b1), .clk(j_k_ff_8_qn), .K(1'b1), .Q(j_k_ff_9_q), .Qn(j_k_ff_9_qn));  // open: preset, en, reset
  J_K_Flip_Flop j_k_ff_10 (
    .J(1'b1), .clk(j_k_ff_9_qn), .K(1'b1), .Q(j_k_ff_10_q), .Qn(j_k_ff_10_qn));  // open: preset, en, reset
  J_K_Flip_Flop j_k_ff_11 (.J(1'b1), .clk(j_k_ff_10_qn), .K(1'b1), .Q(j_k_ff_11_q));  // open: Qn, preset, en, reset
  display_de_7 display_de_7_3 (
    .a(j_k_ff_11_q), .b(j_k_ff_10_q), .c(j_k_ff_9_q), .d(j_k_ff_8_q), .f(display_de_7_3_f),
    .g(display_de_7_3_g));  // open: a_2, b_2, c_2, d_2, e
  _7_Segment_Display u_7_segment_display_3 (.g(display_de_7_3_g), .f(display_de_7_3_f));  // open: a, b, e, d, c, dp

  // Notes on the sheet:
  //   Reset
endmodule

module display_de_7 (
  input  a,
  input  b,
  input  c,
  input  d,
  output a_2,
  output b_2,
  output c_2,
  output d_2,
  output e,
  output f,
  output g
);

  wire and_1_out, and_2_out, and_3_out, and_4_out, and_5_out, and_6_out, and_7_out, and_8_out, and_9_out,
       and_10_out, and_11_out, and_12_out, and_13_out, and_14_out, and_15_out, and_16_out, and_17_out,
       and_18_out, and_19_out, and_20_out, and_21_out, and_22_out, and_23_out, and_24_out, and_25_out,
       and_26_out, and_27_out, and_28_out, and_29_out, and_30_out, and_31_out, and_32_out, and_33_out,
       and_34_out, and_35_out, not_1_out, not_2_out, not_3_out, not_4_out, not_5_out, not_6_out, not_7_out,
       not_8_out, not_9_out, not_10_out, not_11_out, not_12_out, not_13_out, not_14_out, not_15_out,
       not_16_out, not_17_out, not_18_out, not_19_out, not_20_out, not_21_out, not_22_out, not_23_out,
       not_24_out, not_25_out, not_26_out, not_27_out, not_28_out, not_29_out, not_30_out, not_31_out,
       not_32_out, not_33_out, not_34_out, not_35_out, not_36_out, not_37_out, not_38_out, not_39_out,
       not_40_out, not_41_out, not_42_out, not_43_out;

  not not_1 (not_1_out, b);
  and and_1 (and_1_out, not_1_out, not_2_out);
  not not_2 (not_2_out, d);
  not not_3 (not_3_out, a);
  and and_2 (and_2_out, not_3_out, c);
  not not_4 (not_4_out, a);
  and and_3 (and_3_out, not_4_out, b, d);
  and and_4 (and_4_out, b, c);
  and and_5 (and_5_out, a, not_5_out, not_6_out);
  not not_5 (not_5_out, b);
  not not_6 (not_6_out, c);
  and and_6 (and_6_out, a, not_7_out);
  not not_7 (not_7_out, d);
  not not_8 (not_8_out, a);
  and and_7 (and_7_out, not_8_out, not_9_out);
  not not_9 (not_9_out, b);
  not not_10 (not_10_out, a);
  not not_11 (not_11_out, c);
  and and_8 (and_8_out, not_10_out, not_11_out, not_12_out);
  not not_12 (not_12_out, d);
  not not_13 (not_13_out, b);
  and and_9 (and_9_out, not_13_out, not_14_out);
  not not_14 (not_14_out, d);
  not not_15 (not_15_out, a);
  and and_10 (and_10_out, not_15_out, c, d);
  not not_16 (not_16_out, c);
  and and_11 (and_11_out, a, not_16_out, d);
  not not_17 (not_17_out, a);
  and and_12 (and_12_out, not_17_out, not_18_out);
  not not_18 (not_18_out, c);
  not not_19 (not_19_out, a);
  and and_13 (and_13_out, not_19_out, d);
  not not_20 (not_20_out, c);
  and and_14 (and_14_out, not_20_out, d);
  not not_21 (not_21_out, a);
  and and_15 (and_15_out, not_21_out, b);
  and and_16 (and_16_out, a, not_22_out);
  not not_22 (not_22_out, b);
  not not_23 (not_23_out, a);
  and and_17 (and_17_out, not_23_out, not_24_out, not_25_out);
  not not_24 (not_24_out, b);
  not not_25 (not_25_out, d);
  not not_26 (not_26_out, b);
  and and_18 (and_18_out, not_26_out, c, d);
  not not_27 (not_27_out, c);
  and and_19 (and_19_out, b, not_27_out, d);
  and and_20 (and_20_out, b, c, not_28_out);
  not not_28 (not_28_out, d);
  and and_21 (and_21_out, a, not_29_out);
  not not_29 (not_29_out, c);
  not not_30 (not_30_out, b);
  and and_22 (and_22_out, not_30_out, not_31_out);
  not not_31 (not_31_out, d);
  and and_23 (and_23_out, c, not_32_out);
  not not_32 (not_32_out, d);
  and and_24 (and_24_out, a, c);
  and and_25 (and_25_out, a, b);
  not not_33 (not_33_out, c);
  and and_26 (and_26_out, not_33_out, not_34_out);
  not not_34 (not_34_out, d);
  not not_35 (not_35_out, a);
  and and_27 (and_27_out, not_35_out, b, not_36_out);
  not not_36 (not_36_out, c);
  and and_28 (and_28_out, b, not_37_out);
  not not_37 (not_37_out, d);
  and and_29 (and_29_out, a, not_38_out);
  not not_38 (not_38_out, b);
  and and_30 (and_30_out, a, c);
  not not_39 (not_39_out, b);
  and and_31 (and_31_out, not_39_out, c);
  and and_32 (and_32_out, c, not_40_out);
  not not_40 (not_40_out, d);
  not not_41 (not_41_out, a);
  and and_33 (and_33_out, not_41_out, b, not_42_out);
  not not_42 (not_42_out, c);
  and and_34 (and_34_out, a, not_43_out);
  not not_43 (not_43_out, b);
  and and_35 (and_35_out, a, d);
  or or_1 (b_2, and_7_out, and_8_out, and_9_out, and_10_out, and_11_out);
  or or_2 (c_2, and_12_out, and_13_out, and_14_out, and_15_out, and_16_out);
  or or_3 (d_2, and_17_out, and_18_out, and_19_out, and_20_out, and_21_out);
  or or_4 (e, and_22_out, and_23_out, and_24_out, and_25_out);
  or or_5 (f, and_26_out, and_27_out, and_28_out, and_29_out, and_30_out);
  or or_6 (g, and_31_out, and_32_out, and_33_out, and_34_out, and_35_out);
  or or_7 (a_2, and_1_out, and_2_out, and_3_out, and_4_out, and_5_out, and_6_out);
endmodule

module contador (
  output [6:0] out_1,
  output [6:0] out_2,
  output [6:0] out_3,
  output [6:0] out_4,
  output [6:0] out_5
);

  wire and_1_out, and_2_out, and_3_out, and_4_out, and_5_out, clock_1_out, j_k_ff_1_q, j_k_ff_1_qn,
       j_k_ff_2_q, j_k_ff_2_qn, j_k_ff_3_q, j_k_ff_3_qn, j_k_ff_4_q, j_k_ff_5_q, j_k_ff_5_qn, j_k_ff_6_q,
       j_k_ff_6_qn, j_k_ff_7_q, j_k_ff_8_q, j_k_ff_8_qn, j_k_ff_9_q, j_k_ff_9_qn, j_k_ff_10_q, j_k_ff_11_q,
       j_k_ff_11_qn, j_k_ff_12_q, j_k_ff_12_qn, j_k_ff_13_q, j_k_ff_13_qn, j_k_ff_14_q, j_k_ff_14_qn,
       j_k_ff_15_q, j_k_ff_16_q, j_k_ff_16_qn, j_k_ff_17_q, j_k_ff_17_qn, j_k_ff_18_q, j_k_ff_18_qn,
       j_k_ff_19_q, j_k_ff_20_qn, j_k_ff_21_qn, j_k_ff_22_qn, undriven;

  Clock clock_1 (.out(clock_1_out));
  J_K_Flip_Flop j_k_ff_1 (
    .J(1'b1), .clk(clock_1_out), .K(1'b1), .Q(j_k_ff_1_q), .Qn(j_k_ff_1_qn), .reset(and_1_out));  // open: preset, en
  J_K_Flip_Flop j_k_ff_2 (
    .J(1'b1), .clk(j_k_ff_1_qn), .K(1'b1), .Q(j_k_ff_2_q), .Qn(j_k_ff_2_qn), .reset(and_1_out));  // open: preset, en
  J_K_Flip_Flop j_k_ff_3 (
    .J(1'b1), .clk(j_k_ff_2_qn), .K(1'b1), .Q(j_k_ff_3_q), .Qn(j_k_ff_3_qn), .reset(and_1_out));  // open: preset, en
  J_K_Flip_Flop j_k_ff_4 (
    .J(1'b1), .clk(j_k_ff_3_qn), .K(1'b1), .Q(j_k_ff_4_q), .reset(and_1_out));  // open: Qn, preset, en
  and and_1 (and_1_out, j_k_ff_4_q, j_k_ff_2_q);
  display_de_7 display_de_7_1 (
    .a(j_k_ff_4_q), .b(j_k_ff_3_q), .c(j_k_ff_2_q), .d(j_k_ff_1_q), .a_2(out_4[0]), .b_2(out_4[1]),
    .c_2(out_4[2]), .d_2(out_4[3]), .e(out_4[4]), .f(out_4[5]), .g(out_4[6]));
  J_K_Flip_Flop j_k_ff_5 (
    .J(1'b1), .clk(and_1_out), .K(1'b1), .Q(j_k_ff_5_q), .Qn(j_k_ff_5_qn), .reset(and_2_out));  // open: preset, en
  J_K_Flip_Flop j_k_ff_6 (
    .J(1'b1), .clk(j_k_ff_5_qn), .K(1'b1), .Q(j_k_ff_6_q), .Qn(j_k_ff_6_qn), .reset(and_2_out));  // open: preset, en
  J_K_Flip_Flop j_k_ff_7 (
    .J(1'b1), .clk(j_k_ff_6_qn), .K(1'b1), .Q(j_k_ff_7_q), .reset(and_2_out));  // open: Qn, preset, en
  and and_2 (and_2_out, j_k_ff_7_q, j_k_ff_6_q);
  display_de_7 display_de_7_2 (
    .a(1'b0), .b(j_k_ff_7_q), .c(j_k_ff_6_q), .d(j_k_ff_5_q), .a_2(out_5[0]), .b_2(out_5[1]), .c_2(out_5[2]),
    .d_2(out_5[3]), .e(out_5[4]), .f(out_5[5]), .g(out_5[6]));
  J_K_Flip_Flop j_k_ff_8 (
    .J(1'b1), .clk(and_2_out), .K(1'b1), .Q(j_k_ff_8_q), .Qn(j_k_ff_8_qn), .reset(and_3_out));  // open: preset, en
  J_K_Flip_Flop j_k_ff_9 (
    .J(1'b1), .clk(j_k_ff_8_qn), .K(1'b1), .Q(j_k_ff_9_q), .Qn(j_k_ff_9_qn), .reset(and_3_out));  // open: preset, en
  J_K_Flip_Flop j_k_ff_10 (
    .J(1'b1), .clk(j_k_ff_11_qn), .K(1'b1), .Q(j_k_ff_10_q), .reset(and_3_out));  // open: Qn, preset, en
  J_K_Flip_Flop j_k_ff_11 (
    .J(1'b1), .clk(j_k_ff_9_qn), .K(1'b1), .Q(j_k_ff_11_q), .Qn(j_k_ff_11_qn), .reset(and_3_out));  // open: preset, en
  and and_3 (and_3_out, j_k_ff_10_q, j_k_ff_9_q);
  display_de_7 display_de_7_3 (
    .a(j_k_ff_10_q), .b(j_k_ff_11_q), .c(j_k_ff_9_q), .d(j_k_ff_8_q), .a_2(out_2[0]), .b_2(out_2[1]),
    .c_2(out_2[2]), .d_2(out_2[3]), .e(out_2[4]), .f(out_2[5]), .g(out_2[6]));
  J_K_Flip_Flop j_k_ff_12 (
    .J(1'b1), .clk(and_3_out), .K(1'b1), .Q(j_k_ff_12_q), .Qn(j_k_ff_12_qn), .reset(and_4_out));  // open: preset, en
  J_K_Flip_Flop j_k_ff_13 (
    .J(1'b1), .clk(j_k_ff_12_qn), .K(1'b1), .Q(j_k_ff_13_q), .Qn(j_k_ff_13_qn), .reset(and_4_out));  // open: preset, en
  J_K_Flip_Flop j_k_ff_14 (
    .J(1'b1), .clk(j_k_ff_13_qn), .K(1'b1), .Q(j_k_ff_14_q), .Qn(j_k_ff_14_qn), .reset(and_4_out));  // open: preset, en
  J_K_Flip_Flop j_k_ff_15 (
    .J(1'b1), .clk(j_k_ff_14_qn), .K(1'b1), .Q(j_k_ff_15_q), .reset(and_4_out));  // open: Qn, preset, en
  and and_4 (and_4_out, j_k_ff_13_q, j_k_ff_15_q);
  display_de_7 display_de_7_4 (
    .a(j_k_ff_15_q), .b(j_k_ff_14_q), .c(j_k_ff_13_q), .d(j_k_ff_12_q), .a_2(out_3[0]), .b_2(out_3[1]),
    .c_2(out_3[2]), .d_2(out_3[3]), .e(out_3[4]), .f(out_3[5]), .g(out_3[6]));
  J_K_Flip_Flop j_k_ff_16 (
    .J(1'b1), .clk(j_k_ff_17_qn), .K(1'b1), .Q(j_k_ff_16_q), .Qn(j_k_ff_16_qn), .reset(and_5_out));  // open: preset, en
  J_K_Flip_Flop j_k_ff_17 (
    .J(1'b1), .clk(and_4_out), .K(1'b1), .Q(j_k_ff_17_q), .Qn(j_k_ff_17_qn), .reset(and_5_out));  // open: preset, en
  J_K_Flip_Flop j_k_ff_18 (
    .J(1'b1), .clk(j_k_ff_16_qn), .K(1'b1), .Q(j_k_ff_18_q), .Qn(j_k_ff_18_qn), .reset(and_5_out));  // open: preset, en
  J_K_Flip_Flop j_k_ff_19 (
    .J(1'b1), .clk(j_k_ff_18_qn), .K(1'b1), .Q(j_k_ff_19_q), .reset(and_5_out));  // open: Qn, preset, en
  and and_5 (and_5_out, j_k_ff_17_q, j_k_ff_18_q);
  display_de_7 display_de_7_5 (
    .a(j_k_ff_19_q), .b(j_k_ff_18_q), .c(j_k_ff_16_q), .d(j_k_ff_17_q), .a_2(out_1[0]), .b_2(out_1[1]),
    .c_2(out_1[2]), .d_2(out_1[3]), .e(out_1[4]), .f(out_1[5]), .g(out_1[6]));
  J_K_Flip_Flop j_k_ff_20 (.J(1'b1), .clk(j_k_ff_21_qn), .K(1'b1), .Qn(j_k_ff_20_qn));  // open: Q, preset, en, reset
  J_K_Flip_Flop j_k_ff_21 (.J(1'b1), .clk(undriven), .K(1'b1), .Qn(j_k_ff_21_qn));  // open: Q, preset, en, reset
  J_K_Flip_Flop j_k_ff_22 (.J(1'b1), .clk(j_k_ff_20_qn), .K(1'b1), .Qn(j_k_ff_22_qn));  // open: Q, preset, en, reset
  J_K_Flip_Flop j_k_ff_23 (.J(1'b1), .clk(j_k_ff_22_qn), .K(1'b1));  // open: Q, Qn, preset, en, reset

  // Notes on the sheet:
  //   Reset
endmodule
